# Fritzing sketch 3_LED_Button (saved by Fritzing 0.9.3b)
breadboards: 1

parts:
  R1 = Resistor [tolerance=±5% resistance=330 package=THT]
  LED1 = LED - 5mm [color="Red (633nm)" package="5 mm [THT]"]
  Raspberry_Pi_1 = Raspberry Pi 3 [part_number=RPI-3-V1.2]
  LED2 = LED - 5mm [color="Yellow (595nm)" package="5 mm [THT]"]
  R2 = Resistor [tolerance=±5% resistance=330 package=THT]
  LED3 = LED - 5mm [color="Green (560nm)" package="5 mm [THT]"]
  R3 = Resistor [tolerance=±5% resistance=330 package=THT]

nets:
  N1: R1.Pin_0, LED1.cathode
  N2: R1.Pin_1, Raspberry_Pi_1.GND, R2.Pin_1, R3.Pin_1
  N3: LED1.anode, Raspberry_Pi_1.GIPO13
  N4: Raspberry_Pi_1.GIPO19, LED2.anode
  N5: Raspberry_Pi_1.GIPO26, LED3.anode
  N6: LED2.cathode, R2.Pin_0
  N7: LED3.cathode, R3.Pin_0
