# Fritzing sketch Traffic_Light (saved by Fritzing 0.9.3b)
breadboards: 1

parts:
  R1 = Resistor [tolerance=±5% resistance=330 package=THT]
  LED1 = LED - 5mm [color="Red (633nm)" package="5 mm [THT]"]
  Raspberry_Pi_1 = Raspberry Pi 3 [part_number=RPI-3-V1.2]
  LED2 = LED - 5mm [color="Yellow (595nm)" package="5 mm [THT]"]
  R2 = Resistor [tolerance=±5% resistance=330 package=THT]
  LED3 = LED - 5mm [color="Green (560nm)" package="5 mm [THT]"]
  R3 = Resistor [tolerance=±5% resistance=330 package=THT]
  S1 = Pushbutton [package="[THT]"]  # not connected
  S2 = Pushbutton [package="[SMD]"]  # not connected
  S3 = Pushbutton [package="[THT]"]
  J1 = Piezo Speaker

nets:
  N1: R1.Pin_0, LED1.cathode
  N2: R1.Pin_1, Raspberry_Pi_1.GND, R2.Pin_1, R3.Pin_1, S3.Pin_1, S3.Pin_2, J1.pin1
  N3: LED1.anode, Raspberry_Pi_1.GIPO13
  N4: Raspberry_Pi_1.GIPO19, LED2.anode
  N5: Raspberry_Pi_1.GIPO26, LED3.anode
  N6: Raspberry_Pi_1.GIPO21, S3.Pin_3, S3.Pin_4
  N7: Raspberry_Pi_1.GIPO16, J1.pin2
  N8: LED2.cathode, R2.Pin_0
  N9: LED3.cathode, R3.Pin_0

notes:
  GPIO 19
  GPIO 26
  GPIO 13
  GPIO 21
  GPIO 16
